# Fritzing sketch layout (saved by Fritzing 0.9.3b)
stripboards: 3

parts:
  Raspberry_Pi_1 = Raspberry Pi 3 [part_number=RPI-3-V1.2]
  U2 = LCD-16X2 [package=lcd-16x2_nosilk]
  R1 = Resistor [tolerance=±5% resistance=1k package="0805 [SMD]"]
  R2 = Resistor [tolerance=±5% resistance=1k package="0805 [SMD]"]
  RHT1 = Humidity and Temperature Sensor RHT03
  RHT2 = Humidity and Temperature Sensor RHT03
  RHT3 = Humidity and Temperature Sensor RHT03
  R3 = Resistor [tolerance=±5% resistance=10k package="0402 [SMD]"]
  R4 = Resistor [tolerance=±5% resistance=10k package="0402 [SMD]"]
  R5 = Resistor [tolerance=±5% resistance=10k package="0402 [SMD]"]
  S1 = Momentary Switch [package=ksa_sealed_tac_switch]

nets:
  GND: Raspberry_Pi_1.GND, U2.VSS, U2.R_W, U2.K, R1.Pin_1, RHT1.GND_2, RHT2.GND_2, RHT3.GND_2, S1.1
  N1: Raspberry_Pi_1.GIPO17, RHT1.Data-signal, R5.Pin_0
  N2: Raspberry_Pi_1.GIPO27, RHT2.Data-signal, R4.Pin_1
  N3: Raspberry_Pi_1.GIPO22, RHT3.Data-signal, R3.Pin_1
  N4: Raspberry_Pi_1.GIPO11, U2.DB7
  N5: Raspberry_Pi_1.GIPO5, U2.DB6
  N6: Raspberry_Pi_1.GIPO6, U2.DB5
  N7: Raspberry_Pi_1.GIPO13, U2.DB4
  N8: Raspberry_Pi_1.GIPO19, U2.E
  N9: Raspberry_Pi_1.GIPO26, U2.RS
  N10: Raspberry_Pi_1.GIPO21, U2.DB0
  N11: Raspberry_Pi_1.GIPO20, U2.DB1
  N12: Raspberry_Pi_1.GIPO16, U2.DB2
  N13: Raspberry_Pi_1.GIPO12, U2.DB3
  N14: Raspberry_Pi_1.GIPO18, S1.3
  5V: Raspberry_Pi_1.5V, U2.VDD, R2.Pin_0
  N15: U2.VO, R1.Pin_0
  N16: U2.A, R2.Pin_1
  VCC: RHT1.Vcc, RHT2.Vcc, RHT3.Vcc, R3.Pin_0, R4.Pin_0, R5.Pin_1
